# Fritzing sketch Sketch (saved by Fritzing 0.9.10b)
breadboards: 1

parts:
  LCD1 = LCD screen
  Q1 = NPN-Transistor [package="TO92 [THT]"]
  Q2 = NPN-Transistor [package="TO92 [THT]"]
  R1 = Rotary Potentiometer (Small) [maximum_resistance=100kΩ knob_status=50% power=0.5W package=THT]
  LED1 = LED - 5mm [color="Green (570nm)" current=0.030 package="5 mm [THT]"]
  LED2 = LED - 5mm [color="White (4500K)" current=0.030 package="5 mm [THT]"]
  LED3 = LED - 5mm [color="White (4500K)" current=0.030 package="5 mm [THT]"]
  LED4 = LED - 5mm [color="Green (570nm)" current=0.030 package="5 mm [THT]"]
  LED5 = LED - 5mm [color="Green (565nm)" current=0.030 package="5 mm [THT]"]
  LED6 = LED - 5mm [color="White (4500K)" current=0.030 package="5 mm [THT]"]
  LED7 = LED - 5mm [color="White (4500K)" current=0.030 package="5 mm [THT]"]
  LED8 = LED - 5mm [color="Green (570nm)" current=0.030 package="5 mm [THT]"]
  LED9 = LED - 5mm [color="Red (633nm)" current=0.030 package="5 mm [THT]"]
  LED10 = LED - 5mm [color="Red (633nm)" current=0.030 package="5 mm [THT]"]
  LED11 = LED - 5mm [color="Red (633nm)" current=0.030 package="5 mm [THT]"]
  LED12 = LED - 5mm [color="Red (633nm)" current=0.030 package="5 mm [THT]"]
  LED13 = LED - 5mm [color="Blue (470nm)" current=0.030 package="5 mm [THT]"]
  LED14 = LED - 5mm [color="Blue (470nm)" current=0.030 package="5 mm [THT]"]
  LED15 = LED - 5mm [color="Blue (470nm)" current=0.030 package="5 mm [THT]"]
  LED16 = LED - 5mm [color="Blue (470nm)" current=0.030 package="5 mm [THT]"]
  J2 = Basic Servo
  J3 = Basic Servo
  Bauteil1 = Arduino Uno (Rev3)
  J1 = Piezo Speaker
  R2 = Resistor [tolerance=±5% power=0.25 resistance=220 package=THT]

nets:
  GND: LCD1.VSS, LCD1.R/W, LCD1.LED-, R1.leg2, LED1.cathode, LED2.cathode, LED3.cathode, LED4.cathode, LED5.cathode, LED6.cathode, LED7.cathode, LED8.cathode, LED9.cathode, LED10.cathode, LED11.cathode, LED12.cathode, LED13.cathode, LED14.cathode, LED15.cathode, LED16.cathode, J2.gnd, J3.gnd, Bauteil1.GND, J1.pin1
  VCC: LCD1.VDD, Q1.E, Q2.E, R1.leg1, J2.vcc, J3.vcc, Bauteil1.5V, R2.Pin_0
  N1: LCD1.V0, R1.wiper
  N2: LCD1.RS, Bauteil1.D6_PWM
  N3: LCD1.E, Bauteil1.D7
  N4: LCD1.DB4, Bauteil1.D5_PWM
  N5: LCD1.DB5, Bauteil1.D4
  N6: LCD1.DB6, Bauteil1.D3_PWM
  N7: LCD1.DB7, Bauteil1.D2
  N8: LCD1.LED+, R2.Pin_1
  N9: Q1.B, Bauteil1.D11_PWM/MOSI
  N10: Q1.C, LED1.anode, LED2.anode, LED3.anode, LED4.anode, LED5.anode, LED6.anode, LED7.anode, LED8.anode
  N11: Q2.B, Bauteil1.D10_PWM/SS
  N12: Q2.C, LED13.anode, LED14.anode, LED15.anode, LED16.anode
  N13: LED9.anode, LED10.anode, LED11.anode, LED12.anode, Bauteil1.D9_PWM
  N14: J2.pulse, Bauteil1.D12/MISO
  N15: J3.pulse, Bauteil1.D13/SCK
